// Logisim project 8-bit computer.circ as structural Verilog
module main (
  input  [7:0] A,
  input  [7:0] B,
  input  Carry_in,
  input  [2:0] Opcode,
  output A_is_all_zero_s,
  output [7:0] C,
  output Overflow,
  output A_and_B_are_equal,
  output A_is_larger
);

  ALU alu_1 (
    .a(A), .b(B), .CarryIn(Carry_in), .op(Opcode), .a__larger(A_is_larger), .equal(A_and_B_are_equal),
    .Zero(A_is_all_zero_s), .c(C), .CarryOut(Overflow));

  // Notes on the sheet:
  //   000 - Add
  //   001 - Shift Left
  //   011 - NOT
  //   100 - AND
  //   101 - OR
  //   110 - XOR
  //   111 - Compare
  //   010 - Shift Right
endmodule

module ALU (
  input  [7:0] a,
  input  [7:0] b,
  input  CarryIn,
  input  [2:0] op,
  output equal,
  output a__larger,
  output Zero,
  output [7:0] c,
  output CarryOut
);

  wire and_4_out, and_5_out, and_6_out, largeadder_1_carryout, largecomparator_1_a__larger,
       largecomparator_1_equal, lshifter_1_shiftout, n3x8_decoder_1__0_0_0, n3x8_decoder_1__0_0_1,
       n3x8_decoder_1__0_1_0, n3x8_decoder_1__0_1_1, n3x8_decoder_1__1_0_0, n3x8_decoder_1__1_0_1,
       n3x8_decoder_1__1_1_0, n3x8_decoder_1__1_1_1, rshifter_1_shiftout, zero_1_zero;
  wire [7:0] and_1_out, enabler_1_o, enabler_2_o, enabler_3_o, enabler_4_o, enabler_5_o, enabler_6_o,
       enabler_7_o, largeadder_1_sum, largecomparator_1_c, lshifter_1_lshiftout, not_1_out, or_1_out,
       rshifter_1_rshiftout;

  _3x8_decoder u_3x8_decoder_1 (
    .c(op[2]), .b(op[1]), .a(op[0]), ._0_0_0(n3x8_decoder_1__0_0_0), ._0_0_1(n3x8_decoder_1__0_0_1),
    ._0_1_0(n3x8_decoder_1__0_1_0), ._0_1_1(n3x8_decoder_1__0_1_1), ._1_0_0(n3x8_decoder_1__1_0_0),
    ._1_0_1(n3x8_decoder_1__1_0_1), ._1_1_0(n3x8_decoder_1__1_1_0), ._1_1_1(n3x8_decoder_1__1_1_1));
  LargeComparator largecomparator_1 (
    .a(a), .b(b), .equal(largecomparator_1_equal), .a__larger(largecomparator_1_a__larger),
    .c(largecomparator_1_c));
  assign or_1_out = a | b;  // OR_Gate or_1, 8 bits wide
  assign and_1_out = a & b;  // AND_Gate and_1, 8 bits wide
  assign not_1_out = ~a;  // NOT_Gate not_1, 8 bits wide
  LShifter lshifter_1 (
    .LShiftIn(a), .ShiftIn(CarryIn), .ShiftOut(lshifter_1_shiftout), .LShiftOut(lshifter_1_lshiftout));
  RShifter rshifter_1 (
    .RShiftIn(a), .ShiftOut(rshifter_1_shiftout), .ShiftIn(CarryIn), .RShiftOut(rshifter_1_rshiftout));
  LargeAdder largeadder_1 (.CarryIn(CarryIn), .a(a), .b(b), .SUM(largeadder_1_sum), .CarryOut(largeadder_1_carryout));
  and and_2 (equal, largecomparator_1_equal, n3x8_decoder_1__1_1_1);
  and and_3 (a__larger, largecomparator_1_a__larger, n3x8_decoder_1__1_1_1);
  Enabler enabler_1 (.a(largecomparator_1_c), .e(n3x8_decoder_1__1_1_0), .o(enabler_1_o));
  Enabler enabler_2 (.a(or_1_out), .e(n3x8_decoder_1__1_0_1), .o(enabler_2_o));
  Enabler enabler_3 (.a(and_1_out), .e(n3x8_decoder_1__1_0_0), .o(enabler_3_o));
  Enabler enabler_4 (.a(not_1_out), .e(n3x8_decoder_1__0_1_1), .o(enabler_4_o));
  Enabler enabler_5 (.a(lshifter_1_lshiftout), .e(n3x8_decoder_1__0_1_0), .o(enabler_5_o));
  Enabler enabler_6 (.a(rshifter_1_rshiftout), .e(n3x8_decoder_1__0_0_1), .o(enabler_6_o));
  Enabler enabler_7 (.a(largeadder_1_sum), .e(n3x8_decoder_1__0_0_0), .o(enabler_7_o));
  and and_4 (and_4_out, n3x8_decoder_1__0_0_0, largeadder_1_carryout);
  and and_5 (and_5_out, n3x8_decoder_1__0_0_1, rshifter_1_shiftout);
  and and_6 (and_6_out, n3x8_decoder_1__0_1_0, lshifter_1_shiftout);
  assign c = enabler_1_o | enabler_2_o | enabler_3_o | enabler_4_o | enabler_5_o | enabler_6_o | enabler_7_o;  // OR_Gate or_2, 8 bits wide
  or or_3 (CarryOut, and_4_out, and_5_out, and_6_out);
  Zero zero_1 (.BusIn(a), .Zero(zero_1_zero));
  and and_7 (Zero, zero_1_zero, n3x8_decoder_1__1_1_1);
endmodule

module _3x8_decoder (
  input  c,
  input  b,
  input  a,
  output _0_0_0,
  output _0_0_1,
  output _0_1_0,
  output _0_1_1,
  output _1_0_0,
  output _1_0_1,
  output _1_1_0,
  output _1_1_1
);

  wire not_1_out, not_2_out, not_3_out;

  not not_1 (not_1_out, a);
  not not_2 (not_2_out, c);
  not not_3 (not_3_out, b);
  and and_1 (_0_0_0, not_2_out, not_3_out, not_1_out);
  and and_2 (_0_0_1, not_2_out, not_3_out, a);
  and and_3 (_0_1_0, not_2_out, b, not_1_out);
  and and_4 (_0_1_1, not_2_out, b, a);
  and and_5 (_1_0_0, c, not_3_out, not_1_out);
  and and_6 (_1_0_1, c, not_3_out, a);
  and and_7 (_1_1_0, c, b, not_1_out);
  and and_8 (_1_1_1, c, b, a);
endmodule

module LShifter (
  input  ShiftIn,
  input  [7:0] LShiftIn,
  output [7:0] LShiftOut,
  output ShiftOut
);


  assign LShiftOut = {LShiftIn[6:0], ShiftIn};
  assign ShiftOut = LShiftIn[7];
endmodule

module RShifter (
  input  [7:0] RShiftIn,
  input  ShiftIn,
  output ShiftOut,
  output [7:0] RShiftOut
);


  assign RShiftOut = {ShiftIn, RShiftIn[7:1]};
  assign ShiftOut = RShiftIn[0];
endmodule

module HalfAdder (
  input  a,
  input  b,
  output SUM,
  output Carry
);

  xor xor_1 (SUM, a, b);
  and and_1 (Carry, a, b);
endmodule

module FullAdder (
  input  a,
  input  b,
  input  CarryIn,
  output SUM,
  output CarryOut
);

  wire halfadder_1_carry, halfadder_2_carry, halfadder_2_sum;

  HalfAdder halfadder_1 (.a(a), .b(halfadder_2_sum), .SUM(SUM), .Carry(halfadder_1_carry));
  HalfAdder halfadder_2 (.a(b), .b(CarryIn), .SUM(halfadder_2_sum), .Carry(halfadder_2_carry));
  or or_1 (CarryOut, halfadder_1_carry, halfadder_2_carry);
endmodule

module Comparator (
  input  all_bits_above_equal,
  input  a__larger,
  input  a,
  input  b,
  output c,
  output a__larger_2,
  output all_bits_equal_so_far
);

  wire and_2_out, not_1_out;

  xor xor_1 (c, a, b);
  not not_1 (not_1_out, c);
  and and_1 (all_bits_equal_so_far, not_1_out, all_bits_above_equal);
  and and_2 (and_2_out, all_bits_above_equal, a, c);
  or or_1 (a__larger_2, and_2_out, a__larger);
endmodule

module LargeComparator (
  input  [7:0] a,
  input  [7:0] b,
  output [7:0] c,
  output equal,
  output a__larger
);

  wire comparator_1_a__larger_2, comparator_1_all_bits_equal_so_far, comparator_2_a__larger_2,
       comparator_2_all_bits_equal_so_far, comparator_3_a__larger_2, comparator_3_all_bits_equal_so_far,
       comparator_4_a__larger_2, comparator_4_all_bits_equal_so_far, comparator_5_a__larger_2,
       comparator_5_all_bits_equal_so_far, comparator_6_a__larger_2, comparator_6_all_bits_equal_so_far,
       comparator_7_a__larger_2, comparator_7_all_bits_equal_so_far;

  Comparator comparator_1 (
    .a(a[7]), .b(b[7]), .all_bits_above_equal(1'b1), .a__larger(1'b0),
    .all_bits_equal_so_far(comparator_1_all_bits_equal_so_far), .a__larger_2(comparator_1_a__larger_2),
    .c(c[7]));
  Comparator comparator_2 (
    .a(a[6]), .b(b[6]), .all_bits_above_equal(comparator_1_all_bits_equal_so_far),
    .a__larger(comparator_1_a__larger_2), .all_bits_equal_so_far(comparator_2_all_bits_equal_so_far),
    .a__larger_2(comparator_2_a__larger_2), .c(c[6]));
  Comparator comparator_3 (
    .a(a[5]), .b(b[5]), .all_bits_above_equal(comparator_2_all_bits_equal_so_far),
    .a__larger(comparator_2_a__larger_2), .all_bits_equal_so_far(comparator_3_all_bits_equal_so_far),
    .a__larger_2(comparator_3_a__larger_2), .c(c[5]));
  Comparator comparator_4 (
    .a(a[4]), .b(b[4]), .all_bits_above_equal(comparator_3_all_bits_equal_so_far),
    .a__larger(comparator_3_a__larger_2), .all_bits_equal_so_far(comparator_4_all_bits_equal_so_far),
    .a__larger_2(comparator_4_a__larger_2), .c(c[4]));
  Comparator comparator_5 (
    .a(a[3]), .b(b[3]), .all_bits_above_equal(comparator_4_all_bits_equal_so_far),
    .a__larger(comparator_4_a__larger_2), .all_bits_equal_so_far(comparator_5_all_bits_equal_so_far),
    .a__larger_2(comparator_5_a__larger_2), .c(c[3]));
  Comparator comparator_6 (
    .a(a[2]), .b(b[2]), .all_bits_above_equal(comparator_5_all_bits_equal_so_far),
    .a__larger(comparator_5_a__larger_2), .all_bits_equal_so_far(comparator_6_all_bits_equal_so_far),
    .a__larger_2(comparator_6_a__larger_2), .c(c[2]));
  Comparator comparator_7 (
    .a(a[1]), .b(b[1]), .all_bits_above_equal(comparator_6_all_bits_equal_so_far),
    .a__larger(comparator_6_a__larger_2), .all_bits_equal_so_far(comparator_7_all_bits_equal_so_far),
    .a__larger_2(comparator_7_a__larger_2), .c(c[1]));
  Comparator comparator_8 (
    .a(a[0]), .b(b[0]), .all_bits_above_equal(comparator_7_all_bits_equal_so_far),
    .a__larger(comparator_7_a__larger_2), .all_bits_equal_so_far(equal), .a__larger_2(a__larger), .c(c[0]));
endmodule

module Zero (
  input  [7:0] BusIn,
  output Zero
);

  wire or_1_out;

  not not_1 (Zero, or_1_out);
  or or_1 (or_1_out, BusIn[0], BusIn[1], BusIn[2], BusIn[3], BusIn[4], BusIn[5], BusIn[6], BusIn[7]);
endmodule

module Enabler (
  input  [7:0] a,
  input  e,
  output [7:0] o
);

  and and_1 (o[0], a[0], e);
  and and_2 (o[1], a[1], e);
  and and_3 (o[2], a[2], e);
  and and_4 (o[3], a[3], e);
  and and_5 (o[4], a[4], e);
  and and_6 (o[5], a[5], e);
  and and_7 (o[6], a[6], e);
  and and_8 (o[7], a[7], e);
endmodule

module LargeAdder (
  input  CarryIn,
  input  [7:0] a,
  input  [7:0] b,
  output [7:0] SUM,
  output CarryOut
);

  wire fulladder_1_carryout, fulladder_2_carryout, fulladder_3_carryout, fulladder_4_carryout,
       fulladder_5_carryout, fulladder_6_carryout, fulladder_7_carryout;

  FullAdder fulladder_1 (.a(a[0]), .b(b[0]), .CarryIn(CarryIn), .SUM(SUM[0]), .CarryOut(fulladder_1_carryout));
  FullAdder fulladder_2 (
    .a(a[1]), .b(b[1]), .CarryIn(fulladder_1_carryout), .SUM(SUM[1]), .CarryOut(fulladder_2_carryout));
  FullAdder fulladder_3 (
    .a(a[2]), .b(b[2]), .CarryIn(fulladder_2_carryout), .SUM(SUM[2]), .CarryOut(fulladder_3_carryout));
  FullAdder fulladder_4 (
    .a(a[3]), .b(b[3]), .CarryIn(fulladder_3_carryout), .SUM(SUM[3]), .CarryOut(fulladder_4_carryout));
  FullAdder fulladder_5 (
    .a(a[4]), .b(b[4]), .CarryIn(fulladder_4_carryout), .SUM(SUM[4]), .CarryOut(fulladder_5_carryout));
  FullAdder fulladder_6 (
    .a(a[5]), .b(b[5]), .CarryIn(fulladder_5_carryout), .SUM(SUM[5]), .CarryOut(fulladder_6_carryout));
  FullAdder fulladder_7 (
    .a(a[6]), .b(b[6]), .CarryIn(fulladder_6_carryout), .SUM(SUM[6]), .CarryOut(fulladder_7_carryout));
  FullAdder fulladder_8 (.a(a[7]), .b(b[7]), .CarryIn(fulladder_7_carryout), .SUM(SUM[7]), .CarryOut(CarryOut));
endmodule

module _3_Enabler (
  input  a,
  input  e,
  output [2:0] o
);

  wire undriven;

  and and_1 (o[0], undriven, e);
endmodule

module Bus1 (
  input  [7:0] In,
  input  Bus1,
  output [7:0] Out
);

  wire not_1_out;

  and and_1 (Out[7], In[7], not_1_out);
  and and_2 (Out[5], In[5], not_1_out);
  and and_3 (Out[6], In[6], not_1_out);
  and and_4 (Out[4], In[4], not_1_out);
  and and_5 (Out[2], In[2], not_1_out);
  and and_6 (Out[3], In[3], not_1_out);
  not not_1 (not_1_out, Bus1);
  or or_1 (Out[0], In[0], Bus1);
  and and_7 (Out[1], In[1], not_1_out);
endmodule

module Clock (
  input  ClockIn,
  output Clk,
  output Clk_d,
  output Clk_e,
  output Clk_s
);

  wire n6stepper_1__0, n6stepper_1__1, n6stepper_1__2, n6stepper_1__4;

  _6Stepper u_6stepper_1 (
    .reset(n6stepper_1__4), .Clk(ClockIn), ._0(n6stepper_1__0), ._1(n6stepper_1__1), ._2(n6stepper_1__2),
    ._4(n6stepper_1__4));  // open: _3, _5, _6
  or or_1 (Clk, n6stepper_1__1, n6stepper_1__0);
  or or_2 (Clk_d, n6stepper_1__1, n6stepper_1__2);
  or or_3 (Clk_e, Clk, Clk_d);
  and and_1 (Clk_s, Clk, Clk_d);

  // Notes on the sheet:
  //   11001100
  //   01100110
  //   11101110
  //   01000100
endmodule

module _6Stepper (
  input  reset,
  input  Clk,
  output _0,
  output _1,
  output _2,
  output _3,
  output _4,
  output _5,
  output _6
);

  wire memorycell_1_output, memorycell_2_output, memorycell_3_output, memorycell_4_output,
       memorycell_5_output, memorycell_6_output, memorycell_7_output, memorycell_8_output,
       memorycell_9_output, memorycell_10_output, memorycell_11_output, not_1_out, not_2_out, not_3_out,
       not_4_out, not_5_out, not_6_out, not_7_out, not_8_out, or_2_out, or_3_out;

  or or_1 (_0, reset, not_2_out);
  not not_1 (not_1_out, Clk);
  not not_2 (not_2_out, memorycell_2_output);
  MemoryCell memorycell_1 (.Input(not_3_out), .Set(or_2_out), .Output(memorycell_1_output));
  not not_3 (not_3_out, reset);
  or or_2 (or_2_out, reset, not_1_out);
  or or_3 (or_3_out, reset, Clk);
  MemoryCell memorycell_2 (.Input(memorycell_1_output), .Set(or_3_out), .Output(memorycell_2_output));
  MemoryCell memorycell_3 (.Input(memorycell_2_output), .Set(or_2_out), .Output(memorycell_3_output));
  and and_1 (_1, memorycell_2_output, not_4_out);
  not not_4 (not_4_out, memorycell_4_output);
  MemoryCell memorycell_4 (.Input(memorycell_3_output), .Set(or_3_out), .Output(memorycell_4_output));
  and and_2 (_2, memorycell_4_output, not_5_out);
  not not_5 (not_5_out, memorycell_6_output);
  MemoryCell memorycell_5 (.Input(memorycell_4_output), .Set(or_2_out), .Output(memorycell_5_output));
  MemoryCell memorycell_6 (.Input(memorycell_5_output), .Set(or_3_out), .Output(memorycell_6_output));
  and and_3 (_3, memorycell_6_output, not_6_out);
  not not_6 (not_6_out, memorycell_8_output);
  MemoryCell memorycell_7 (.Input(memorycell_6_output), .Set(or_2_out), .Output(memorycell_7_output));
  and and_4 (_4, memorycell_8_output, not_7_out);
  not not_7 (not_7_out, memorycell_11_output);
  MemoryCell memorycell_8 (.Input(memorycell_7_output), .Set(or_3_out), .Output(memorycell_8_output));
  MemoryCell memorycell_9 (.Input(memorycell_8_output), .Set(or_2_out), .Output(memorycell_9_output));
  MemoryCell memorycell_10 (.Input(memorycell_11_output), .Set(or_2_out), .Output(memorycell_10_output));
  MemoryCell memorycell_11 (.Input(memorycell_9_output), .Set(or_3_out), .Output(memorycell_11_output));
  and and_5 (_5, memorycell_11_output, not_8_out);
  not not_8 (not_8_out, _6);
  MemoryCell memorycell_12 (.Input(memorycell_10_output), .Set(or_3_out), .Output(_6));
endmodule

module MemoryCell (
  input  Input,
  input  Set,
  output Output
);

  wire and_1_out, and_2_out, not_1_out;

  and and_1 (and_1_out, Set, Input);
  and and_2 (and_2_out, Set, not_1_out);
  not not_1 (not_1_out, Input);
  S_R_Flip_Flop #(.trigger("low")) s_r_ff_1 (
    .S(and_1_out), .clk(1'b0), .R(and_2_out), .Q(Output));  // open: Qn, preset, reset, en
endmodule

// IR
module Byte (
  input  [7:0] Input,
  input  Set,
  output [7:0] Output
);

  MemoryCell memorycell_1 (.Input(Input[0]), .Set(Set), .Output(Output[0]));
  MemoryCell memorycell_2 (.Input(Input[1]), .Set(Set), .Output(Output[1]));
  MemoryCell memorycell_3 (.Input(Input[2]), .Set(Set), .Output(Output[2]));
  MemoryCell memorycell_4 (.Input(Input[3]), .Set(Set), .Output(Output[3]));
  MemoryCell memorycell_5 (.Input(Input[4]), .Set(Set), .Output(Output[4]));
  MemoryCell memorycell_6 (.Input(Input[5]), .Set(Set), .Output(Output[5]));
  MemoryCell memorycell_7 (.Input(Input[6]), .Set(Set), .Output(Output[6]));
  MemoryCell memorycell_8 (.Input(Input[7]), .Set(Set), .Output(Output[7]));
endmodule

module Register (
  input  [7:0] Input,
  input  s,
  input  e,
  output [7:0] Output
);

  wire [7:0] byte_1_output;

  Byte byte_1 (.Input(Input), .Set(s), .Output(byte_1_output));
  Enabler enabler_1 (.a(byte_1_output), .e(e), .o(Output));
endmodule

module CPU (
  input  [7:0] BusIn,
  output [2:0] ALU,
  output IAR,
  output Bus1,
  output MAR,
  output ACC,
  output RAM,
  output RAM_2,
  output ACC_2,
  output TMP,
  output R0,
  output R0_2,
  output R1,
  output R1_2,
  output R2,
  output R2_2,
  output R3,
  output R3_2,
  output IAR_2
);

  wire aluinstructionselect_1_acc, aluinstructionselect_1_reg_a, aluinstructionselect_1_reg_b,
       aluinstructionselect_1_reg_b_2, clock_1_out, clock_2_clk, clock_2_clk_e, clock_2_clk_s, IR_out,
       n6stepper_1__1, n6stepper_1__2, n6stepper_1__3, n6stepper_1__4, n6stepper_1__5, n6stepper_1__6,
       regselect_1_r0, regselect_1_r0_2, regselect_1_r1, regselect_1_r1_2, regselect_1_r2, regselect_1_r2_2,
       regselect_1_r3, regselect_1_r3_2;
  wire [7:0] byte_1_output;

  Clock_part clock_1 (.out(clock_1_out));
  and and_1 (RAM, n6stepper_1__1, clock_2_clk_e);
  and and_2 (ACC_2, n6stepper_1__2, clock_2_clk_e);
  and and_3 (R0, regselect_1_r0_2, clock_2_clk_e);
  and and_4 (R1, regselect_1_r1_2, clock_2_clk_e);
  and and_5 (R2, regselect_1_r2_2, clock_2_clk_e);
  and and_6 (R3, regselect_1_r3_2, clock_2_clk_e);
  and and_7 (IAR_2, Bus1, clock_2_clk_e);
  Clock clock_2 (
    .ClockIn(clock_1_out), .Clk(clock_2_clk), .Clk_e(clock_2_clk_e), .Clk_s(clock_2_clk_s));  // open: Clk_d
  Byte byte_1 (.Input(BusIn), .Set(IR_out), .Output(byte_1_output));
  _6Stepper u_6stepper_1 (
    .reset(n6stepper_1__6), .Clk(clock_2_clk), ._0(Bus1), ._1(n6stepper_1__1), ._2(n6stepper_1__2),
    ._3(n6stepper_1__3), ._4(n6stepper_1__4), ._5(n6stepper_1__5), ._6(n6stepper_1__6));
  RegSelect regselect_1 (
    .RegB_2(aluinstructionselect_1_reg_b_2), .R0_2(regselect_1_r0_2), .R1_2(regselect_1_r1_2),
    .R2_2(regselect_1_r2_2), .R3_2(regselect_1_r3_2), .Clk_e(clock_2_clk_e), .Clk_s(clock_2_clk_s),
    ._4(byte_1_output[4]), ._5(byte_1_output[5]), ._6(byte_1_output[6]), ._7(byte_1_output[7]),
    .RegB(aluinstructionselect_1_reg_b), .RegA(aluinstructionselect_1_reg_a), .R0(regselect_1_r0),
    .R1(regselect_1_r1), .R2(regselect_1_r2), .R3(regselect_1_r3));
  ALUinstructionSelect aluinstructionselect_1 (
    .Reg_B(aluinstructionselect_1_reg_b), .Reg_A(aluinstructionselect_1_reg_a), .ALU(ALU),
    .IR_0_1_2_3({byte_1_output[0], byte_1_output[1], byte_1_output[2], byte_1_output[3]}),
    .Stepper3(n6stepper_1__3), .Stepper4(n6stepper_1__4), .Stepper5(n6stepper_1__5),
    .ACC(aluinstructionselect_1_acc), .Reg_B_2(aluinstructionselect_1_reg_b_2));  // open: ACC_2, TMP
  and and_8 (IAR, n6stepper_1__2, clock_2_clk_s);
  and and_9 (MAR, Bus1, clock_2_clk_s);
  and and_10 (ACC, Bus1, clock_2_clk_s);
  buf and_11 (RAM_2, clock_2_clk_s);  // AND_Gate
  buf and_12 (TMP, clock_2_clk_s);  // AND_Gate
  and and_13 (R0_2, regselect_1_r0, clock_2_clk_s);
  and and_14 (R1_2, regselect_1_r1, clock_2_clk_s);
  and and_15 (R2_2, regselect_1_r2, clock_2_clk_s);
  and and_16 (R3_2, regselect_1_r3, clock_2_clk_s);
  and IR (IR_out, n6stepper_1__1, clock_2_clk_s);

  // Notes on the sheet:
  //   All Enables
  //   All Sets
endmodule

module _2x4Decoder (
  input  a,
  input  b,
  output _0_0,
  output _0_1,
  output _1_0,
  output _1_1
);

  wire not_1_out, not_2_out;

  not not_1 (not_1_out, a);
  not not_2 (not_2_out, b);
  and and_1 (_0_0, not_1_out, not_2_out);
  and and_2 (_0_1, a, not_2_out);
  and and_3 (_1_0, not_1_out, b);
  and and_4 (_1_1, a, b);
endmodule

module RegSelect (
  input  Clk_e,
  input  Clk_s,
  input  RegB,
  input  RegB_2,
  input  RegA,
  input  _4,
  input  _5,
  input  _6,
  input  _7,
  output R0,
  output R1,
  output R0_2,
  output R2,
  output R1_2,
  output R3,
  output R2_2,
  output R3_2
);

  wire and_1_out, and_2_out, and_3_out, and_4_out, and_5_out, and_6_out, and_7_out, and_8_out,
       n2x4decoder_1__0_0, n2x4decoder_1__0_1, n2x4decoder_1__1_0, n2x4decoder_1__1_1, n2x4decoder_2__0_0,
       n2x4decoder_2__0_1, n2x4decoder_2__1_0, n2x4decoder_2__1_1, n2x4decoder_3__0_0, n2x4decoder_3__0_1,
       n2x4decoder_3__1_0, n2x4decoder_3__1_1;

  or or_1 (R0_2, and_1_out, and_5_out);
  or or_2 (R1_2, and_2_out, and_6_out);
  or or_3 (R2_2, and_3_out, and_7_out);
  or or_4 (R3_2, and_4_out, and_8_out);
  and and_1 (and_1_out, Clk_e, RegB, n2x4decoder_1__0_0);
  and and_2 (and_2_out, Clk_e, RegB, n2x4decoder_1__0_1);
  and and_3 (and_3_out, Clk_e, RegB, n2x4decoder_1__1_0);
  and and_4 (and_4_out, Clk_e, RegB, n2x4decoder_1__1_1);
  and and_5 (and_5_out, Clk_e, RegA, n2x4decoder_2__0_0);
  and and_6 (and_6_out, Clk_e, RegA, n2x4decoder_2__0_1);
  and and_7 (and_7_out, Clk_e, RegA, n2x4decoder_2__1_0);
  and and_8 (and_8_out, Clk_e, RegA, n2x4decoder_2__1_1);
  _2x4Decoder u_2x4decoder_1 (
    .a(_7), .b(_6), ._0_0(n2x4decoder_1__0_0), ._0_1(n2x4decoder_1__0_1), ._1_0(n2x4decoder_1__1_0),
    ._1_1(n2x4decoder_1__1_1));
  _2x4Decoder u_2x4decoder_2 (
    .a(_5), .b(_4), ._0_0(n2x4decoder_2__0_0), ._0_1(n2x4decoder_2__0_1), ._1_0(n2x4decoder_2__1_0),
    ._1_1(n2x4decoder_2__1_1));
  _2x4Decoder u_2x4decoder_3 (
    .a(_7), .b(_6), ._0_0(n2x4decoder_3__0_0), ._0_1(n2x4decoder_3__0_1), ._1_0(n2x4decoder_3__1_0),
    ._1_1(n2x4decoder_3__1_1));
  and and_9 (R0, Clk_s, RegB_2, n2x4decoder_3__0_0);
  and and_10 (R1, Clk_s, RegB_2, n2x4decoder_3__0_1);
  and and_11 (R2, Clk_s, RegB_2, n2x4decoder_3__1_0);
  and and_12 (R3, Clk_s, RegB_2, n2x4decoder_3__1_1);
endmodule

module ALUinstructionSelect (
  input  Stepper3,
  input  Stepper4,
  input  Stepper5,
  input  [3:0] IR_0_1_2_3,
  output Reg_B,
  output TMP,
  output Reg_A,
  output ACC,
  output ACC_2,
  output Reg_B_2,
  output [2:0] ALU
);

  wire and_6_out, not_1_out;

  and and_1 (ALU[0], Stepper4, IR_0_1_2_3[3], IR_0_1_2_3[0]);
  and and_2 (ALU[1], Stepper4, IR_0_1_2_3[3], IR_0_1_2_3[1]);
  and and_3 (ALU[2], Stepper4, IR_0_1_2_3[3], IR_0_1_2_3[2]);
  and and_4 (Reg_B, Stepper3, IR_0_1_2_3[3]);
  and and_5 (ACC, Stepper4, IR_0_1_2_3[3]);
  and and_6 (and_6_out, IR_0_1_2_3[0], IR_0_1_2_3[1], IR_0_1_2_3[2]);
  and and_7 (ACC_2, Stepper5, IR_0_1_2_3[3], not_1_out);
  not not_1 (not_1_out, and_6_out);

  assign Reg_A = ACC;
  assign Reg_B_2 = ACC_2;
  assign TMP = Reg_B;

  // Notes on the sheet:
  //   Enables
  //   Sets
endmodule

module OtherInstructionSelect (
  input  [3:0] IR_0_1_2_3
);

  wire undriven, undriven_2, undriven_3;

  _3x8_decoder u_3x8_decoder_1 (
    .c(undriven), .b(undriven_2), .a(undriven_3));  // open: _0_0_0, _0_0_1, _0_1_0, _0_1_1, _1_0_0, _1_0_1, _1_1_0, _1_1_1
endmodule
